# Fritzing sketch Circuit (saved by Fritzing 0.9.2b)
breadboards: 1

parts:
  Part1 = Arduino Nano (Rev3.0)
  DFPlayer_Mini1 = DFPlayer MINI [package="DIP (Dual Inline) [THT]"]
  Part2 = HX711 Weighing Sensor Module
  J1 = female pin header, 4 pins [form="♀ (female)"]
  R1 = Resistor [tolerance=±5% resistance=1k package="0603 [SMD]"]
  DS1 = DS18B20 1-Wire Temperature Sensor [part_number=DS18B20]
  R2 = Resistor [tolerance=±5% resistance=4.7k package="0603 [SMD]"]

nets:
  GND: Part1.GND, DFPlayer_Mini1.GND#9, Part2.GND, DS1.GND
  N1: Part1.D2, DS1.DQ, R2.Pin_1
  N2: Part1.D10, R1.Pin_0
  N3: Part1.D11/MOSI, DFPlayer_Mini1.TX
  VCC: Part1.5V, DFPlayer_Mini1.VCC, Part2.VCC, DS1.VDD, R2.Pin_0
  N4: Part1.A1, Part2.CK/TX
  N5: Part1.A0, Part2.DO/RX
  N6: DFPlayer_Mini1.RX, R1.Pin_1
  N7: Part2.E+, J1.pin4
  N8: Part2.E-, J1.pin3
  N9: Part2.A+, J1.pin2
  N10: Part2.A-, J1.pin1

notes:
  Load Cell

custom parts:
  DFPlayer MINI: MP3 module by DFRobot.com for playing Music from an SD-Card. Supports WAV and MP3 files.
